# Fritzing sketch BlinkOnChipKit (saved by Fritzing 0.9.0b)
breadboards: 1

parts:
  LED1 = LED - 5mm [color="Red (633nm)" package="5 mm [THT]"]
  LED2 = LED - 5mm [color="Red (633nm)" package="5 mm [THT]"]
  LED3 = LED - 5mm [color="Red (633nm)" package="5 mm [THT]"]
  R1 = Resistor [tolerance=±5% resistance=220 package=THT]
  R2 = Resistor [tolerance=±5% resistance=220 package=THT]
  R3 = Resistor [tolerance=±5% resistance=220 package=THT]
  Uno1 = chipKIT Uno32 [package="SIP (Single Inline) [THT]"]

nets:
  N1: LED1.cathode, LED2.cathode, LED3.cathode, Uno1.GND
  N2: LED1.anode, R1.Pin_0
  N3: LED2.anode, R2.Pin_0
  N4: LED3.anode, R3.Pin_0
  N5: R1.Pin_1, Uno1.D11
  N6: R2.Pin_1, Uno1.D12
  N7: R3.Pin_1, Uno1.D13

custom parts:
  chipKIT Uno32: Arduino-compatible prototyping platform
