# Fritzing sketch BlinkOnESP8266 (saved by Fritzing 0.9.1b)
breadboards: 1

parts:
  Part1 = FTDI Basic Programmer
  U1 = ESP8266 WiFi Module [part_number=ESP8266]
  S1 = Momentary Switch [package=ksa_sealed_tac_switch]

nets:
  N1: Part1.DTR, U1.RST
  N2: Part1.RXI, U1.TXD
  N3: Part1.TXO, U1.RXD
  N4: Part1.POWER, U1.VCC, U1.CH_PD
  GND: Part1.GND, U1.GND, S1.1
  N5: U1.GPIO_0, S1.3

notes:
  PROG
  FTDI
  ESP8266 ESP-01

custom parts:
  ESP8266 WiFi Module: Generic WiFi Module based on the ESP8266 with onboard PCB antenna and UART communications
