# Fritzing sketch BlinkOnMSP430 (saved by Fritzing 0.9.0b)
breadboards: 1

parts:
  LED1 = LED - 5mm [color="Red (633nm)" package="5 mm [THT]"]
  LED2 = LED - 5mm [color="Red (633nm)" package="5 mm [THT]"]
  LED3 = LED - 5mm [color="Red (633nm)" package="5 mm [THT]"]
  R1 = Resistor [tolerance=±5% resistance=220 package=THT]
  R2 = Resistor [tolerance=±5% resistance=220 package=THT]
  R3 = Resistor [tolerance=±5% resistance=220 package=THT]
  J1 = Generic double row female header - 12 pins [form="♀ (female)" package=THT]

nets:
  N1: LED1.cathode, LED2.cathode, LED3.cathode, J1.pin7
  N2: LED1.anode, R1.Pin_0
  N3: LED2.anode, R2.Pin_0
  N4: LED3.anode, R3.Pin_0
  N5: R1.Pin_1, J1.pin4
  N6: R2.Pin_1, J1.pin5
  N7: R3.Pin_1, J1.pin6

custom parts:
  Generic double row female header - 12 pins: Generic double row female header
