# Fritzing sketch BlinkOnRaspberryPi (saved by Fritzing 0.9.0b)
breadboards: 1

parts:
  LED1 = LED - 5mm [color="Red (633nm)" package="5 mm [THT]"]
  LED2 = LED - 5mm [color="Red (633nm)" package="5 mm [THT]"]
  LED3 = LED - 5mm [color="Red (633nm)" package="5 mm [THT]"]
  R1 = Resistor [tolerance=±5% resistance=220 package=THT]
  R2 = Resistor [tolerance=±5% resistance=220 package=THT]
  R3 = Resistor [tolerance=±5% resistance=220 package=THT]
  Raspberry_Pi_B_rev1 = Raspberry Pi B rev1

nets:
  N1: LED1.cathode, LED2.cathode, LED3.cathode, Raspberry_Pi_B_rev1.GND
  N2: LED1.anode, R1.Pin_0
  N3: LED2.anode, R2.Pin_0
  N4: LED3.anode, R3.Pin_0
  N5: R1.Pin_1, Raspberry_Pi_B_rev1.GPIO_22
  N6: R2.Pin_1, Raspberry_Pi_B_rev1.GPIO_21
  N7: R3.Pin_1, Raspberry_Pi_B_rev1.GPIO_17
