# Fritzing sketch EncoderOnArduino (saved by Fritzing 0.9.1b)
breadboards: 1

parts:
  Part1 = Arduino Uno (Rev3)
  R1 = Resistor [tolerance=±5% resistance=10k package=THT]
  R2 = Resistor [tolerance=±5% resistance=10k package=THT]
  R3 = Resistor [tolerance=±5% resistance=10k package=THT]
  R4 = Resistor [tolerance=±5% resistance=10k package=THT]
  RE1 = Rotary Encoder [package=THT]
  RE2 = Rotary Encoder [package=THT]

nets:
  N1: Part1.D9_PWM, R4.Pin_0, RE1.EncoderPinB
  N2: Part1.D10_PWM/SS, R2.Pin_0, RE1.EncoderPinA
  N3: Part1.D11_PWM/MOSI, R3.Pin_0, RE2.EncoderPinB
  N4: Part1.D12/MISO, R1.Pin_0, RE2.EncoderPinA
  N5: Part1.5V, R1.Pin_1, R2.Pin_1, R3.Pin_1, R4.Pin_1
  N6: Part1.GND, RE1.EncoderPinC, RE2.EncoderPinC
