# Fritzing sketch KeyerOnArduino (saved by Fritzing 0.9.0b)
breadboards: 1

parts:
  J1 = Piezo Speaker
  U1 = 3.5mm Audio Jack [package=audio-jack-3.5mm-smd]
  R1 = Resistor [tolerance=±5% resistance=6.8k package="0805 [SMD]"]
  R2 = Resistor [tolerance=±5% resistance=6.8k package="0805 [SMD]"]
  Q1 = NPN-Transistor [package="TO92 [THT]"]
  R3 = Resistor [tolerance=±5% resistance=6.8k package=THT]  # not connected
  Part2 = Arduino Uno (Rev3)

nets:
  N1: J1.pin1, Q1.C
  N2: J1.pin2, R1.Pin_1, R2.Pin_1, Part2.5V
  N3: U1.RIGHT, R2.Pin_0, Part2.D6_PWM
  N4: U1.SLEEVE, Q1.E, Part2.GND
  N5: U1.LEFT, R1.Pin_0, Part2.D7
