# Fritzing sketch KeyerOnChipKit (saved by Fritzing 0.9.1b)
breadboards: 1

parts:
  J1 = Piezo Speaker
  U1 = 3.5mm Audio Jack [package=audio-jack-3.5mm-smd]
  R2 = Resistor [tolerance=±5% resistance=6.8k package="0805 [SMD]"]
  Q1 = NPN-Transistor [package="TO92 [THT]"]
  R3 = Resistor [tolerance=±5% resistance=6.8k package=THT]  # not connected
  Uno1 = chipKIT Uno32 [package="SIP (Single Inline) [THT]"]
  R1 = Resistor [tolerance=±5% resistance=6.8k package="0805 [SMD]"]

nets:
  N1: J1.pin1, Q1.C
  N2: J1.pin2, R2.Pin_1, Uno1.5V, R1.Pin_1
  N3: U1.RIGHT, R2.Pin_0, Uno1.D6
  N4: U1.SLEEVE, Q1.E, Uno1.GND
  N5: U1.LEFT, Uno1.D7, R1.Pin_0

custom parts:
  chipKIT Uno32: Arduino-compatible prototyping platform
