# Fritzing sketch KeyerOnMSP430 (saved by Fritzing 0.9.0b)
breadboards: 1

parts:
  J1 = Piezo Speaker
  U1 = 3.5mm Audio Jack [package=audio-jack-3.5mm-smd]
  R1 = Resistor [tolerance=±5% resistance=6.8k package="0805 [SMD]"]
  R2 = Resistor [tolerance=±5% resistance=6.8k package="0805 [SMD]"]
  Q1 = NPN-Transistor [package="TO92 [THT]"]
  R3 = Resistor [tolerance=±5% resistance=6.8k package=THT]  # not connected
  J2 = Generic double row female header - 12 pins [form="♀ (female)" package=THT]
  Launchpad1 = TI Launchpad MSP430G2

nets:
  N1: J1.pin1, Q1.C
  N2: J1.pin2, R1.Pin_1, R2.Pin_1, Launchpad1.p9
  N3: U1.RIGHT, R2.Pin_0, J2.pin6
  N4: U1.SLEEVE, Q1.E, Launchpad1.p8
  N5: U1.LEFT, R1.Pin_0, J2.pin5

custom parts:
  Generic double row female header - 12 pins: Generic double row female header
  TI Launchpad MSP430G2: The LaunchPad is an easy-to-use, affordable, and scalable introduction to the world of microcontrollers and the MSP430 family. See: http://e2e.ti.com/group/msp430launchpad/w/default.aspx
