# Fritzing sketch KeyerOnPIC32 (saved by Fritzing 0.9.0b)
breadboards: 1

parts:
  J1 = Piezo Speaker
  U1 = 3.5mm Audio Jack [package=audio-jack-3.5mm-smd]
  R1 = Resistor [tolerance=±5% resistance=6.8k package="0805 [SMD]"]
  R2 = Resistor [tolerance=±5% resistance=6.8k package="0805 [SMD]"]
  Q1 = NPN-Transistor [package="TO92 [THT]"]
  R3 = Resistor [tolerance=±5% resistance=6.8k package=THT]
  J2 = Generic double row female header - 12 pins [form="♀ (female)" package=THT]

nets:
  N1: J1.pin1, Q1.C
  N2: J1.pin2, R1.Pin_1, R2.Pin_1, J2.pin1
  N3: U1.RIGHT, R2.Pin_0, J2.pin5
  N4: U1.SLEEVE, Q1.E, J2.pin10
  N5: U1.LEFT, R1.Pin_0, J2.pin12
  N6: Q1.B, R3.Pin_0
  N7: R3.Pin_1, J2.pin11

custom parts:
  Generic double row female header - 12 pins: Generic double row female header
