# Fritzing sketch LcdOnArduino (saved by Fritzing 0.9.1b)
breadboards: 1

parts:
  LCD1 = LCD screen
  Part1 = Arduino Uno (Rev3)
  R1 = TRIMPOT [package=trim_pot_pth]
  R2 = TRIMPOT [package=trim_pot_pth]

nets:
  VSS: LCD1.VSS, Part1.GND, R1.CCW
  VDD: LCD1.VDD, Part1.5V, R2.CCW
  N1: LCD1.V0, R1.CW
  N2: LCD1.RS, Part1.D2
  N3: LCD1.E, Part1.D3_PWM
  N4: LCD1.DB4, Part1.D9_PWM
  N5: LCD1.DB5, Part1.D10_PWM/SS
  N6: LCD1.DB6, Part1.D11_PWM/MOSI
  N7: LCD1.DB7, Part1.D12/MISO
  N8: LCD1.LED+, R2.CW
