# Fritzing sketch LcdOnPIC32 (saved by Fritzing 0.9.1b)
breadboards: 1

parts:
  LCD1 = LCD screen
  R1 = TRIMPOT [package=trim_pot_pth]
  R2 = TRIMPOT [package=trim_pot_pth]
  J1 = PIC32 J10 Pins 1 to 28 [form="♀ (female)" package=THT]

nets:
  N1: LCD1.VSS, R1.CCW, J1.pin2
  N2: LCD1.VDD, R2.CCW, J1.pin_28
  N3: LCD1.V0, R1.CW
  N4: LCD1.RS, J1.pin12
  N5: LCD1.E, J1.pin11
  N6: LCD1.DB4, J1.pin10
  N7: LCD1.DB5, J1.pin9
  N8: LCD1.DB6, J1.pin8
  N9: LCD1.DB7, J1.pin7
  N10: LCD1.LED+, R2.CW

custom parts:
  PIC32 J10 Pins 1 to 28: Generic double row female header
