# Fritzing sketch MatrixOnArduino (saved by Fritzing 0.9.1b)
breadboards: 1

parts:
  Part1 = Arduino Uno (Rev3)
  R1 = Resistor [tolerance=±5% resistance=10k package=THT]
  R2 = Resistor [tolerance=±5% resistance=10k package=THT]
  R3 = Resistor [tolerance=±5% resistance=10k package=THT]
  KEYPAD1 = Membrane Matrix Keypad

nets:
  N1: Part1.D2, R2.Pin_0, KEYPAD1.6
  N2: Part1.D3_PWM, R3.Pin_0, KEYPAD1.5
  N3: Part1.D4, R1.Pin_0, KEYPAD1.4
  N4: Part1.D5_PWM, KEYPAD1.3
  N5: Part1.D6_PWM, KEYPAD1.2
  N6: Part1.D7, KEYPAD1.1
  N7: Part1.5V, R1.Pin_1, R2.Pin_1, R3.Pin_1

custom parts:
  Membrane Matrix Keypad: Membrane Matrix 3x4 Keypad
