# Fritzing sketch MatrixOnPIC32 (saved by Fritzing 0.9.1b)
breadboards: 1

parts:
  R1 = Resistor [tolerance=±5% resistance=10k package=THT]
  R2 = Resistor [tolerance=±5% resistance=10k package=THT]
  R3 = Resistor [tolerance=±5% resistance=10k package=THT]
  KEYPAD1 = Membrane Matrix Keypad
  J2 = PIC32 J10 Pins 1 to 28 [form="♀ (female)" package=THT]

nets:
  N1: R1.Pin_0, KEYPAD1.4, J2.pin_18
  N2: R1.Pin_1, R2.Pin_1, R3.Pin_1, J2.pin_28
  N3: R2.Pin_0, KEYPAD1.6, J2.pin_20
  N4: R3.Pin_0, KEYPAD1.5, J2.pin_19
  N5: KEYPAD1.1, J2.pin5
  N6: KEYPAD1.2, J2.pin7
  N7: KEYPAD1.3, J2.pin9

custom parts:
  Membrane Matrix Keypad: Membrane Matrix 3x4 Keypad
  PIC32 J10 Pins 1 to 28: Generic double row female header
