# Fritzing sketch SwitchOnArduino (saved by Fritzing 0.9.1b)
breadboards: 1

parts:
  R1 = Resistor [tolerance=±5% resistance=220 package=THT]
  R2 = Resistor [tolerance=±5% resistance=220 package=THT]
  Part1 = Arduino Uno (Rev3)
  S2 = Pushbutton [package="[THT]"]
  S3 = Pushbutton [package="[THT]"]

nets:
  N1: R1.Pin_0, Part1.D3_PWM, S2.Pin_1, S2.Pin_2
  N2: R1.Pin_1, R2.Pin_1, Part1.5V
  N3: R2.Pin_0, Part1.D2, S3.Pin_1, S3.Pin_2
  N4: Part1.GND, S2.Pin_3, S2.Pin_4, S3.Pin_3, S3.Pin_4
