# Fritzing sketch SwitchOnPIC32 (saved by Fritzing 0.9.1b)
breadboards: 1

parts:
  J2 = Generic double row female header - 12 pins [form="♀ (female)" package=THT]
  S1 = Momentary Switch [package=ksa_sealed_tac_switch]
  S2 = Momentary Switch [package=ksa_sealed_tac_switch]
  R2 = Resistor [tolerance=±5% resistance=10k package=THT]
  R3 = Resistor [tolerance=±5% resistance=10k package=THT]

nets:
  N1: J2.pin5, S1.4
  N2: J2.pin7, R2.Pin_0, R3.Pin_0
  N3: J2.pin10, S1.1, S2.1
  N4: J2.pin12, S2.4
  N5: S1.3, R3.Pin_1
  N6: S2.3, R2.Pin_1

custom parts:
  Generic double row female header - 12 pins: Generic double row female header
